# Fritzing sketch schematic (saved by Fritzing 1.0.0rc)
perfboards: 1

parts:
  M1 = DOIT Esp32 DevKit v1 (30 pins long, 11 pins width) [part_number=ESP32S-PIN30]
  J1 = female pin header, 2 pins [form="♀ (female)"]
  J2 = female pin header, 2 pins [form="♀ (female)"]
  J3 = female pin header, 2 pins [form="♀ (female)"]
  J4 = female pin header, 3 pins [form="♀ (female)"]
  R1 = Resistor [tolerance=±5% resistance=4.7k package="0402 [SMD]"]
  J5 = female pin header, 2 pins [form="♀ (female)"]
  R2 = Resistor [tolerance=±5% resistance=10k package="0402 [SMD]"]

nets:
  N1: M1.3V3, J4.pin2, R1.Pin_1
  N2: M1.GND, J4.pin3, J5.pin1
  N3: M1.D32, J4.pin1, R1.Pin_0
  N4: M1.D33, J5.pin2, R2.Pin_0
  N5: M1.D27, R2.Pin_1
  N6: M1.D14, J3.pin2
  N7: M1.D13, J2.pin2
  N8: M1.VIN, J1.pin2

notes:
  rain sensor
  anemometer
  + 5V
  raing gauge
  dallas temperature

custom parts:
  DOIT Esp32 DevKit v1 (30 pins long, 11 pins width): The DOIT Esp32 DevKit v1 is one of the development board created by DOIT to evaluate the ESP-WROOM-32 module. It is based on the ESP32 microcontroller that boasts Wifi, Bluetooth, Ethernet and Low Power support all in a single chip. (vanepp) made breadboard work, adjusted pin numbering and labels and reduced size of schematic and cleaned up pcb. This chip is 30pins long (2 x15) and 11 pins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
